# Fritzing sketch HuehnerStallMitLichtSensorSchaltplan (saved by Fritzing 0.9.3b)
breadboards: 1

parts:
  Bauteil1 = Arduino Mega 2560 (Rev3)
  S1 = Pushbutton [package=THT]
  S2 = Pushbutton [package=THT]
  S3 = Pushbutton [package=THT]
  LED1 = LED - 5mm [color="Blue (430nm)" package="5 mm [THT]"]
  R1 = Resistor [tolerance=±5% resistance=220 package=THT]
  R2 = Resistor [tolerance=±5% resistance=100 package=THT]
  R3 = Resistor [tolerance=±5% resistance=100 package=THT]
  R4 = PHOTOCELL [package=photocell-kit]
  KY-1 = Keyes Relay [package=THT]
  KY-2 = Keyes Relay [package=THT]
  M1 = DC Motor
  R5 = Resistor [tolerance=±5% resistance=10k package=THT]
  R6 = Resistor [tolerance=±5% resistance=10k package=THT]

nets:
  N1: Bauteil1.A0, KY-1.power
  N2: Bauteil1.A3, S2.leg1, R6.Pin_1
  N3: Bauteil1.A5, R4.P$1, R5.Pin_1
  N4: Bauteil1.GND, R1.Pin_1, R2.Pin_1, R3.Pin_0, KY-1.ground, KY-1.NC, KY-2.ground, KY-2.NC, R5.Pin_0, R6.Pin_0
  N5: Bauteil1.D13_PWM, LED1.cathode, R1.Pin_0
  N6: Bauteil1.D12_PWM, KY-2.power
  N7: Bauteil1.5V, S1.leg0, S2.leg0, S3.leg1, R4.P$2, KY-1.signal, KY-1.NO, KY-2.signal, KY-2.NO
  N8: Bauteil1.D4_PWM, S3.leg0, R2.Pin_0
  N9: Bauteil1.D7_PWM, S1.leg1, R3.Pin_1
  N10: KY-1.C, M1.pin_1
  N11: KY-2.C, M1.pin_2

custom parts:
  Keyes Relay: The Keyes 5V relay module is suitable for SCM development, home appliance control. It uses a 5V~12V TIL control signal which can control DC / AC signal.
